// Logisim project Cache.circ as structural Verilog: 5 circuits, main circuit main
module main (
  input  [15:0] in_1,
  input  in_2,
  input  [9:0] ADDRESS
);

  wire clock, j_k_ff_1_q, not_1_out, store;
  wire [15:0] data, data1, data2, data3, data4, outputcache, outputmp;

  Clock clock_1 (.out(clock));
  not not_1 (not_1_out, store);
  J_K_Flip_Flop j_k_ff_1 (.J(store), .clk(clock), .K(not_1_out), .Q(j_k_ff_1_q));  // open: Qn, preset, en, reset
  MP Memoria_Principal (
    .inputData(in_1), .store(in_2), .address(ADDRESS), .outputData(data1), .outputData_2(data2),
    .outputData_3(data3), .outputData_4(data4));
  Controle_cache ControleCache (.row(ADDRESS[4:2]), .cacheStatus(store), .Tag(ADDRESS[9:5]), .store(j_k_ff_1_q));
  Cache Memoria_Cache (
    .input1(data1), .input2(data2), .input3(data3), .input4(data4), .row(ADDRESS[4:2]), .word(ADDRESS[1:0]),
    .store(store), .out_8(outputcache));
  Multiplexer #(.select(2), .width(16), .enable("false")) multiplexer_1 (
    .in0(data1), .in1(data2), .in2(data3), .in3(data4), .out(outputmp), .sel(ADDRESS[1:0]));
  Multiplexer #(.width(16), .enable("false")) multiplexer_2 (
    .in0(outputcache), .in1(outputmp), .out(data), .sel(store));

  // Other names for the same wires on the sheet: word[1:0] = ADDRESS[1:0]; row[2:0] = ADDRESS[4:2];
  //   tag[4:0] = ADDRESS[9:5]

  // Notes on the sheet:
  //   STALL
  //   Store = 1 => PC - 1
endmodule

module MP (
  input  [15:0] inputData,
  input  store,
  input  [9:0] address,
  output [15:0] outputData,
  output [15:0] outputData_2,
  output [15:0] outputData_3,
  output [15:0] outputData_4
);

  wire CLK, demultiplexer_1_out0, demultiplexer_1_out1, demultiplexer_1_out2, demultiplexer_1_out3,
       not_1_out, not_2_out, not_3_out, not_4_out;

  Clock clock_1 (.out(CLK));
  Demultiplexer #(.select(2), .enable("false")) demultiplexer_1 (
    .out0(demultiplexer_1_out0), .out1(demultiplexer_1_out1), .out2(demultiplexer_1_out2),
    .out3(demultiplexer_1_out3), .in(store), .sel(address[1:0]));
  assign outputData = demultiplexer_1_out0 ? inputData : 16'bz;  // Controlled_Buffer controlled_buffer_1
  assign outputData_2 = demultiplexer_1_out1 ? inputData : 16'bz;  // Controlled_Buffer controlled_buffer_2
  assign outputData_3 = demultiplexer_1_out2 ? inputData : 16'bz;  // Controlled_Buffer controlled_buffer_3
  assign outputData_4 = demultiplexer_1_out3 ? inputData : 16'bz;  // Controlled_Buffer controlled_buffer_4
  not not_1 (not_1_out, demultiplexer_1_out0);
  not not_2 (not_2_out, demultiplexer_1_out1);
  not not_3 (not_3_out, demultiplexer_1_out2);
  not not_4 (not_4_out, demultiplexer_1_out3);
  RAM #(.dataWidth(16)) ram_1 (.addr(address[9:2]), .data(outputData), .clk(CLK), .ld(not_1_out));  // open: sel, clr
  RAM #(.dataWidth(16)) ram_2 (.addr(address[9:2]), .data(outputData_2), .clk(CLK), .ld(not_2_out));  // open: sel, clr
  RAM #(.dataWidth(16)) ram_3 (.addr(address[9:2]), .data(outputData_3), .clk(CLK), .ld(not_3_out));  // open: sel, clr
  RAM #(.dataWidth(16)) ram_4 (.addr(address[9:2]), .data(outputData_4), .clk(CLK), .ld(not_4_out));  // open: sel, clr
endmodule

module Linha (
  input  [15:0] inputData1,
  input  [15:0] inputData2,
  input  [15:0] inputData3,
  input  store,
  input  [1:0] word,
  input  [15:0] inputData4,
  output [15:0] \output 
);

  wire CLK;
  wire [15:0] output1, output2, output3, output4;

  Clock clock_1 (.out(CLK));
  Register #(.width(16)) register_1 (.D(inputData1), .en(store), .Q(output1), .clk(CLK));  // open: clr
  Register #(.width(16)) register_2 (.D(inputData2), .en(store), .Q(output2), .clk(CLK));  // open: clr
  Register #(.width(16)) register_3 (.D(inputData3), .en(store), .Q(output3), .clk(CLK));  // open: clr
  Register #(.width(16)) register_4 (.D(inputData4), .en(store), .Q(output4), .clk(CLK));  // open: clr
  Multiplexer #(.select(2), .width(16), .enable("false")) multiplexer_1 (
    .in0(output1), .in1(output2), .in2(output3), .in3(output4), .out(\output ), .sel(word));
endmodule

module Cache (
  input  [15:0] input1,
  input  [15:0] input2,
  input  [15:0] input3,
  input  [15:0] input4,
  input  [2:0] row,
  input  [1:0] word,
  input  store,
  output [15:0] out_8
);

  wire row1, row2, row3, row4, row5, row6, row7, row8;
  wire [15:0] output1, output2, output3, output4, output5, output6, output7, output8;

  Demultiplexer #(.select(3), .enable("false")) demultiplexer_1 (
    .out0(row1), .out1(row2), .out2(row3), .out3(row4), .out4(row5), .out5(row6), .out6(row7), .out7(row8),
    .in(store), .sel(row));
  Linha linha_1 (
    .inputData1(input1), .inputData2(input2), .inputData3(input3), .store(row1), .word(word),
    .inputData4(input4), .\output (output1));
  Linha linha_2 (
    .inputData1(input1), .inputData2(input2), .inputData3(input3), .store(row2), .word(word),
    .inputData4(input4), .\output (output2));
  Linha linha_3 (
    .inputData1(input1), .inputData2(input2), .inputData3(input3), .store(row3), .word(word),
    .inputData4(input4), .\output (output3));
  Linha linha_4 (
    .inputData1(input1), .inputData2(input2), .inputData3(input3), .store(row4), .word(word),
    .inputData4(input4), .\output (output4));
  Linha linha_5 (
    .inputData1(input1), .inputData2(input2), .inputData3(input3), .store(row5), .word(word),
    .inputData4(input4), .\output (output5));
  Linha linha_6 (
    .inputData1(input1), .inputData2(input2), .inputData3(input3), .store(row6), .word(word),
    .inputData4(input4), .\output (output6));
  Linha linha_7 (
    .inputData1(input1), .inputData2(input2), .inputData3(input3), .store(row7), .word(word),
    .inputData4(input4), .\output (output7));
  Linha linha_8 (
    .inputData1(input1), .inputData2(input2), .inputData3(input3), .store(row8), .word(word),
    .inputData4(input4), .\output (output8));
  Multiplexer #(.select(3), .width(16), .enable("false")) multiplexer_1 (
    .in0(output1), .in1(output2), .in2(output3), .in3(output4), .in4(output5), .in5(output6), .in6(output7),
    .in7(output8), .out(out_8), .sel(row));

  // Other names for the same wires on the sheet: word1[15:0] = input1; word2[15:0] = input2; word3[15:0] = input3;
  //   word4[15:0] = input4
endmodule

// CC
module Controle_cache (
  input  [4:0] Tag,
  input  store,
  input  [2:0] row,
  output cacheStatus
);

  wire CLK, comparator_1_eq, not_1_out;
  wire [5:0] bit_extender_1_out, controlled_buffer_1_out, Tag_t;

  Clock clock_1 (.out(CLK));
  Adder #(.width(6)) adder_1 (.a(6'b000001), .b(bit_extender_1_out), .out(Tag_t));  // open: cin, cout
  assign bit_extender_1_out = {{1{1'b0}}, Tag};  // Bit_Extender bit_extender_1
  assign controlled_buffer_1_out = store ? Tag_t : 6'bz;  // Controlled_Buffer controlled_buffer_1
  not not_1 (not_1_out, store);
  RAM #(.addrWidth(3), .dataWidth(6)) ram_1 (
    .addr(row), .data(controlled_buffer_1_out), .clk(CLK), .ld(not_1_out));  // open: sel, clr
  Comparator #(.width(6)) comparator_1 (.a(controlled_buffer_1_out), .b(Tag_t), .eq(comparator_1_eq));  // open: gt, lt
  not not_2 (cacheStatus, comparator_1_eq);

  // Notes on the sheet:
  //   Soma 1 a tag para ignorar a Tag 0
  //   Armazena a Tag
  //   CacheStatus:
  //   0 - Cache Hit
  //   1 - Cache Miss
endmodule
